# Fritzing sketch receiverDiagram (saved by Fritzing 0.9.3b)
breadboards: 1

parts:
  Part1 = Arduino Nano (Rev3.0)
  Part2 = Bluetooth HC-05 Macho  # not connected
  VCC1 = Battery block 9V
  S1 = H-Bridge with L298N
  M1 = DC Motor
  M2 = DC Motor
  M3 = DC Motor
  M4 = DC Motor
  S2 = H-Bridge with L298N
  VCC2 = Battery block 9V
  VCC3 = Battery block 9V

nets:
  GND: Part1.GND, VCC1.-, S1.GND, S2.GND, VCC2.-, VCC3.-
  N1: Part1.D2, S2.IN1
  N2: Part1.D3, S2.IN2
  N3: Part1.D4, S2.IN3
  N4: Part1.D5, S2.IN4
  N5: Part1.D6, S1.IN1
  N6: Part1.D7, S1.IN2
  N7: Part1.D8, S1.IN3
  N8: Part1.D9, S1.IN4
  5V: Part1.3V3, VCC1.+, S1.5V, S2.5V
  N9: S1.12V, VCC2.+
  N10: S1.M1-01, M2.pin_2
  N11: S1.M1-02, M2.pin_1
  N12: S1.M2-01, M3.pin_2
  N13: S1.M2-02, M3.pin_1
  N14: M1.pin_1, S2.M2-02
  N15: M1.pin_2, S2.M2-01
  N16: M4.pin_1, S2.M1-02
  N17: M4.pin_2, S2.M1-01
  N18: S2.12V, VCC3.+

custom parts:
  H-Bridge with L298N: h-bridge
