# Fritzing sketch transmitter (saved by Fritzing 0.9.3b)

parts:
  GY1 = MPU-6050 Board GY-521 [form="♀ (female)" package=THT]
  Part1 = Lilypad Arduino Board
  Part2 = Bluetooth HC-05 Macho
  VCC1 = 4 x AAA Battery Mount

nets:
  VCC: GY1.pin1, Part1.VCC, Part2.VCC, VCC1.+
  GND: GY1.pin2, Part1.GND, Part2.GND, VCC1.-
  N1: GY1.pin3, Part1.A5
  N2: GY1.pin4, Part1.A4
  N3: GY1.pin8, Part1.D2
  N4: Part1.D10, Part2.TXD
  N5: Part1.MOSI/D11, Part2.RXD

notes:
  --NOTE---
  YOU CAN USE ANY BATTERIES WITH A MAXIMUM OF 5.5V

custom parts:
  MPU-6050 Board GY-521: Acelerometro y Giroscopio MPU-6050 Board GY-521
